# Fritzing sketch wiring (saved by Fritzing 1.0.5)

parts:
  A1 = XIAO ESP32C3-tht
  Adafruit#1 = Adafruit LSM6DS3TR-C [part_number=4503]
  BAT1 = LIPO-110mAh [package=lipo-110]
  S1 = Pushbutton [package="[THT]"]
  S2 = Pushbutton [package="[THT]"]
  S3 = SPST Switch [package=switch-spdt-smd]

nets:
  N1: A1.Pin_2, A1.Pin_21, Adafruit#1.GND, S1.Pin_1, S1.Pin_2
  N2: A1.Pin_7, BAT1.-
  N3: A1.Pin_8, S3.P
  N4: A1.Pin_11, S2.Pin_3, S2.Pin_4
  N5: A1.Pin_12, S1.Pin_4
  N6: A1.Pin_13, Adafruit#1.SDA
  N7: A1.Pin_14, Adafruit#1.SCL
  N8: A1.Pin_20, Adafruit#1.3.3V
  N9: BAT1.+, S3.O

custom parts:
  XIAO ESP32C3-tht: Seeed Studio XIAO ESP32C3 adopts new RISC-V architecture, supporting both Wi-Fi and BLE wireless connectivities.
  Adafruit LSM6DS3TR-C: Add motion and orientation sensing to your Arduino project with this affordable 6 Degree of Freedom (6-DoF) sensor with sensors from ST. The board includes an ST LSM6DS3TR-C, a great entry-level 6-DoF IMU accelerometer + gyro. The 3-axis accelerometer can tell you which direction is down towards the Earth (by measuring gravity) or how fast the board is accelerating in 3D space. The 3-axis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
